// Logisim project projet1.circ as structural Verilog: 4 circuits, main circuit ordinateur
// 8
module ordinateur (
);

  wire clock_1_out, \Définir_le_comportement_de_cette_composante_out_ctrl_instructions ;
  wire [1:0] \Définir_le_comportement_de_cette_composante_out_ctrl_data ;
  wire [3:0] \Définir_le_comportement_de_cette_composante_out_adr_data ;
  wire [7:0] \Définir_le_comportement_de_cette_composante_out_adr_instructions ,
       \Définir_le_comportement_de_cette_composante_out_data_data , ram_1_data, rom_1_data;

  ROM rom_1 (
    .addr(\Définir_le_comportement_de_cette_composante_out_adr_instructions ), .data(rom_1_data),
    .sel(\Définir_le_comportement_de_cette_composante_out_ctrl_instructions ));
  microprocesseur \Définir_le_comportement_de_cette_composante  (
    .in_data_instructions(rom_1_data), .in_data_data(ram_1_data),
    .out_ctrl_instructions(\Définir_le_comportement_de_cette_composante_out_ctrl_instructions ),
    .out_adr_instructions(\Définir_le_comportement_de_cette_composante_out_adr_instructions ),
    .out_ctrl_data(\Définir_le_comportement_de_cette_composante_out_ctrl_data ),
    .out_data_data(\Définir_le_comportement_de_cette_composante_out_data_data ),
    .out_adr_data(\Définir_le_comportement_de_cette_composante_out_adr_data ));
  Clock clock_1 (.out(clock_1_out));
  RAM #(.addrWidth(4), .bus("separate")) ram_1 (
    .addr(\Définir_le_comportement_de_cette_composante_out_adr_data ),
    .din(\Définir_le_comportement_de_cette_composante_out_data_data ), .data(ram_1_data),
    .str(\Définir_le_comportement_de_cette_composante_out_ctrl_data [1]), .clk(clock_1_out),
    .ld(\Définir_le_comportement_de_cette_composante_out_ctrl_data [0]));  // open: sel, clr

  // Notes on the sheet:
  //   mémoire d'instructions
  //   contents of rom_1 (hex, n*v repeats v):
  //   5 59 5 6 86 5e 5 13 97 63 a aa 66 f 9 b7 6b c a 88 88 5 f 9b 97 cc 6c 5 a 10 d4 d8 70 14 31 d1 e5 75
  //   34 5 f1 79
  //   Normalement, ce circuit ne devrait pas
  //   nécessiter de modifications.
  //   Ouvrir 'microprocesseur' à gauche (sous projet1)
  //   mémoire de données
endmodule

module microprocesseur (
  input  [7:0] in_data_instructions,
  input  [7:0] in_data_data,
  output [7:0] out_adr_instructions,
  output out_ctrl_instructions,
  output [1:0] out_ctrl_data,
  output [3:0] out_adr_data,
  output [7:0] out_data_data
);

  wire clock_1_out, decoder_1_bypass_alu, decoder_1_write_to_rx;
  wire [1:0] decoder_1_rx_number, decoder_1_ry_number;
  wire [2:0] decoder_1_alu_operation;
  wire [7:0] alu_gif_3000_1_p2, alu_gif_3000_1_p4, multiplexer_1_out, register_1_q, register_2_q,
       registre_NPC_q;

  Clock clock_1 (.out(clock_1_out));
  not not_1 (out_ctrl_instructions, clock_1_out);
  Register #(.trigger("high")) register_1 (
    .D(in_data_instructions), .en(1'b1), .Q(register_1_q), .clk(out_ctrl_instructions), .clr(1'b0));
  Pull_Resistor pull_resistor_1 (.node(in_data_instructions));
  Counter registre_NPC (
    .load(1'b0), .D({8{1'b0}}), .count(1'b1), .Q(registre_NPC_q), .clk(out_ctrl_instructions), .clr(1'b0));  // open: carry
  Register #(.trigger("high")) register_2 (
    .D(in_data_data), .en(1'b1), .Q(register_2_q), .clk(out_ctrl_instructions), .clr(1'b0));
  Pull_Resistor pull_resistor_2 (.node(in_data_data));
  Register Registre_PC (
    .D(registre_NPC_q), .en(1'b1), .Q(out_adr_instructions), .clk(out_ctrl_instructions), .clr(1'b0));
  Decoder decoder_1 (
    .Instruction(register_1_q), .Bypass_ALU(decoder_1_bypass_alu), .Data_Memory_Address(out_adr_data),
    .Ry_number(decoder_1_ry_number), .Data_Memory_Control(out_ctrl_data),
    .ALU_Operation(decoder_1_alu_operation), .Rx_number(decoder_1_rx_number),
    .Write_to_Rx(decoder_1_write_to_rx));
  // ALU_GIF_3000 alu_gif_3000_1: pin names not known; wires that end beside it: out_data_data, alu_gif_3000_1_p2, decoder_1_alu_operation, alu_gif_3000_1_p4
  // Probe on decoder_1_alu_operation
  Multiplexer #(.width(8), .enable("false")) multiplexer_1 (
    .in0(alu_gif_3000_1_p4), .in1(register_2_q), .out(multiplexer_1_out), .sel(decoder_1_bypass_alu));
  Register_File register_file_1 (
    .New_Rx_Value(multiplexer_1_out), .Write_To_Rx(decoder_1_write_to_rx), .Ry_Address(decoder_1_rx_number),
    .Rx_address(decoder_1_ry_number), .Clk_in(out_ctrl_instructions), .Rx_Value(out_data_data),
    .Ry_Value(alu_gif_3000_1_p2));

  // Notes on the sheet:
  //   ALU GIF-3000
  //   Instruction Fetch
  //   Instruction Decode
  //   EXecute
  //   MEMory Access
  //   Write Back
endmodule

module Decoder (
  input  [7:0] Instruction,
  output [1:0] Ry_number,
  output [1:0] Rx_number,
  output [3:0] Data_Memory_Address,
  output [2:0] ALU_Operation,
  output Bypass_ALU,
  output [1:0] Data_Memory_Control,
  output Write_to_Rx
);

  wire [1:0] and_2_out;

  and and_1 (and_2_out[1], Instruction[6], ~Instruction[7]);  // AND_Gate
  and and_2 (and_2_out[0], ~Instruction[6], ~Instruction[7]);  // AND_Gate
  not not_1 (Bypass_ALU, Instruction[7]);
  assign Data_Memory_Control = and_2_out;  // Buffer buffer_1, 2 bits wide
  not not_2 (Write_to_Rx, and_2_out[1]);

  assign ALU_Operation = Instruction[6:4];
  assign Data_Memory_Address = Instruction[5:2];
  assign Rx_number = Instruction[3:2];
  assign Ry_number = Instruction[1:0];
endmodule

module Register_File (
  input  [7:0] New_Rx_Value,
  input  Write_To_Rx,
  input  [1:0] Ry_Address,
  input  [1:0] Rx_address,
  input  Clk_in,
  output [7:0] Rx_Value,
  output [7:0] Ry_Value
);

  wire [3:0] demultiplexer_1_out0;
  wire [7:0] register_1_q, register_2_q, register_3_q, register_4_q;

  Demultiplexer #(.select(2)) demultiplexer_1 (
    .out0(demultiplexer_1_out0[0]), .out1(demultiplexer_1_out0[1]), .out2(demultiplexer_1_out0[2]),
    .out3(demultiplexer_1_out0[3]), .in(Write_To_Rx), .sel(Rx_address), .en(1'b1));
  Register #(.trigger("falling")) register_1 (
    .D(New_Rx_Value), .en(demultiplexer_1_out0[0]), .Q(register_1_q), .clk(Clk_in), .clr(1'b0));
  Register #(.trigger("falling")) register_2 (
    .D(New_Rx_Value), .en(demultiplexer_1_out0[1]), .Q(register_2_q), .clk(Clk_in), .clr(1'b0));
  Register #(.trigger("falling")) register_3 (
    .D(New_Rx_Value), .en(demultiplexer_1_out0[2]), .Q(register_3_q), .clk(Clk_in), .clr(1'b0));
  Register #(.trigger("falling")) register_4 (
    .D(New_Rx_Value), .en(demultiplexer_1_out0[3]), .Q(register_4_q), .clk(Clk_in), .clr(1'b0));
  Multiplexer #(.select(2), .width(8), .enable("false")) multiplexer_1 (
    .in0(register_1_q), .in1(register_2_q), .in2(register_3_q), .in3(register_4_q), .out(Rx_Value),
    .sel(Rx_address));
  Multiplexer #(.select(2), .width(8), .enable("false")) multiplexer_2 (
    .in0(register_1_q), .in1(register_2_q), .in2(register_3_q), .in3(register_4_q), .out(Ry_Value),
    .sel(Ry_Address));
endmodule
