// Logisim project proj final.circ as structural Verilog: 1 circuit, main circuit main
module main (
  input  B,
  input  A
);

  wire and_1_out, and_2_out, and_3_out, and_4_out, and_5_out, and_6_out, and_7_out, and_8_out, and_9_out,
       BaA_out, BonAoQ0_out, BxA_anQ0_out, BxA_out, clock_1_out, demultiplexer_1_out0, demultiplexer_1_out1,
       demultiplexer_1_out2, demultiplexer_1_out3, demultiplexer_1_out4, demultiplexer_1_out5,
       demultiplexer_1_out6, demultiplexer_1_out7, demultiplexer_2_out0, demultiplexer_2_out1,
       demultiplexer_2_out2, demultiplexer_2_out3, demultiplexer_2_out4, demultiplexer_2_out5,
       demultiplexer_2_out6, demultiplexer_2_out7, multiplexer_1_out, multiplexer_2_out, multiplexer_3_out,
       multiplexer_4_out, multiplexer_5_out, multiplexer_6_out, not_1_out, not_2_out, not_3_out, not_4_out,
       not_5_out, or_1_out, or_2_out, or_3_out, or_4_out, or_5_out, or_6_out, or_7_out, Q0xA_out, Q0xB_out;
  wire [2:0] n74163_1_p10;
  wire [2:2] n74163_1_p13;

  Clock clock_1 (.out(clock_1_out));
  not not_1 (not_1_out, A);
  not not_2 (not_2_out, B);
  xor Q0xB (Q0xB_out, n74163_1_p10[0], B);
  xor BxA (BxA_out, B, A);
  xnor Q0xA (Q0xA_out, n74163_1_p10[0], A);
  or BaA (BaA_out, B, A);
  or BonAoQ0 (BonAoQ0_out, B, not_1_out, n74163_1_p10[0]);
  and and_1 (and_1_out, not_2_out, A);
  not not_3 (not_3_out, n74163_1_p10[0]);
  and and_2 (and_2_out, n74163_1_p10[0], BaA_out);
  and and_3 (and_3_out, BxA_out, not_3_out);
  and and_4 (and_4_out, B, A);
  and and_5 (and_5_out, not_2_out, n74163_1_p10[0], A);
  and and_6 (and_6_out, n74163_1_p10[0], not_1_out, B);
  and BxA_anQ0 (BxA_anQ0_out, not_3_out, BxA_out);
  or or_1 (or_1_out, Q0xB_out, Q0xA_out);
  or or_2 (or_2_out, not_3_out, BxA_out);
  or or_3 (or_3_out, not_1_out, not_2_out);
  or or_4 (or_4_out, n74163_1_p10[0], and_4_out);
  or or_5 (or_5_out, not_3_out, and_4_out);
  and and_7 (and_7_out, not_3_out, A);
  and and_8 (and_8_out, and_1_out, not_3_out);
  and and_9 (and_9_out, not_3_out, or_3_out);
  or or_6 (or_6_out, and_5_out, and_7_out);
  or or_7 (or_7_out, and_7_out, and_6_out);
  Multiplexer #(.select(3)) multiplexer_1 (
    .in0(BxA_anQ0_out), .in1(or_1_out), .in2(or_2_out), .in3(and_2_out), .in4(BonAoQ0_out), .in5(and_3_out),
    .in6(or_3_out), .in7(and_9_out), .out(multiplexer_1_out), .sel({n74163_1_p13[2], n74163_1_p10[2:1]}),
    .en(1'b1));
  Multiplexer #(.select(3)) multiplexer_2 (
    .in0(or_7_out), .in1(1'b1), .in2(A), .in3(or_4_out), .in4(1'b1), .in5(or_6_out), .in6(1'b1),
    .in7(or_5_out), .out(multiplexer_2_out), .sel({n74163_1_p13[2], n74163_1_p10[2:1]}), .en(1'b1));
  Multiplexer #(.select(3)) multiplexer_3 (
    .in0(A), .in1(1'b1), .in2(not_3_out), .in3(1'b0), .in4(and_6_out), .in5(B), .in6(1'b1), .in7(1'b1),
    .out(multiplexer_3_out), .sel({n74163_1_p13[2], n74163_1_p10[2:1]}), .en(1'b1));
  Multiplexer #(.select(3)) multiplexer_4 (
    .in0(B), .in1(1'b0), .in2(and_1_out), .in3(1'b1), .in4(1'b1), .in5(1'b0), .in6(1'b1), .in7(1'b1),
    .out(multiplexer_4_out), .sel({n74163_1_p13[2], n74163_1_p10[2:1]}), .en(1'b1));
  Multiplexer #(.select(3)) multiplexer_5 (
    .in0(A), .in1(1'b0), .in2(and_8_out), .in3(1'b1), .in4(1'b1), .in5(B), .in6(1'b0), .in7(1'b0),
    .out(multiplexer_5_out), .sel({n74163_1_p13[2], n74163_1_p10[2:1]}), .en(1'b1));
  Multiplexer #(.select(3)) multiplexer_6 (
    .in0(B), .in1(1'b0), .in2(and_1_out), .in3(1'b0), .in4(and_6_out), .in5(1'b0), .in6(1'b1), .in7(1'b1),
    .out(multiplexer_6_out), .sel({n74163_1_p13[2], n74163_1_p10[2:1]}), .en(1'b1));
  not not_4 (not_4_out, multiplexer_1_out);
  // _74163 74163_1: pin names not known; wires that end beside it: multiplexer_3_out, multiplexer_4_out, multiplexer_5_out, multiplexer_6_out, multiplexer_2_out, 1'b1, not_4_out, 1'b1, clock_1_out, n74163_1_p10[0], n74163_1_p10[1], n74163_1_p10[2], n74163_1_p13[2], n74163_1_p10
  Demultiplexer #(.select(3)) demultiplexer_1 (
    .out0(demultiplexer_1_out0), .out1(demultiplexer_1_out1), .out2(demultiplexer_1_out2),
    .out3(demultiplexer_1_out3), .out4(demultiplexer_1_out4), .out5(demultiplexer_1_out5),
    .out6(demultiplexer_1_out6), .out7(demultiplexer_1_out7), .in(not_5_out), .sel(n74163_1_p10), .en(1'b1));
  not not_5 (not_5_out, n74163_1_p13[2]);
  Demultiplexer #(.select(3)) demultiplexer_2 (
    .out0(demultiplexer_2_out0), .out1(demultiplexer_2_out1), .out2(demultiplexer_2_out2),
    .out3(demultiplexer_2_out3), .out4(demultiplexer_2_out4), .out5(demultiplexer_2_out5),
    .out6(demultiplexer_2_out6), .out7(demultiplexer_2_out7), .in(n74163_1_p13[2]), .sel(n74163_1_p10),
    .en(1'b1));
  LED led_1 (.in(demultiplexer_1_out0));
  LED led_2 (.in(demultiplexer_1_out5));
  LED led_3 (.in(demultiplexer_2_out2));
  LED led_4 (.in(demultiplexer_2_out7));
  LED led_5 (.in(demultiplexer_1_out2));
  LED led_6 (.in(demultiplexer_1_out1));
  LED led_7 (.in(demultiplexer_1_out6));
  LED led_8 (.in(demultiplexer_1_out7));
  LED led_9 (.in(demultiplexer_2_out3));
  LED led_10 (.in(demultiplexer_2_out4));
  LED led_11 (.in(demultiplexer_1_out3));
  LED led_12 (.in(demultiplexer_1_out4));
  LED led_13 (.in(demultiplexer_2_out0));
  LED led_14 (.in(demultiplexer_2_out1));
  LED led_15 (.in(demultiplexer_2_out5));
  LED led_16 (.in(demultiplexer_2_out6));

  // Notes on the sheet:
  //   Load
  //   Count
  //   D1
  //   D2
  //   D3
  //   D0
endmodule
