// Logisim project projet final génial clair testé.circ as structural Verilog: 1 circuit, main circuit main
module main (
  input  B,
  input  A,
  output [3:0] out_3
);

  wire A_nQ0_B_nA_Q0_out, A_nQ0_out, B_A__Q0_out, B_A_nQ0_out, B_A_out, B_nA__nQ0_out, B_nA_out,
       B_nA_Q0_2_out, B_nA_Q0_out, BxA_nQ0_2_out, BxA_nQ0_out, BxA_out, clock_1_out, multiplexer_1_out,
       multiplexer_2_out, multiplexer_3_out, n74163_1_p7, n74163_1_p9, n74163_1_p11, nB_A__Q0__B_nA__nQ0_out,
       nB_A__Q0_out, nB_A_out, nB_A_Q0_A_nQ0_out, nB_A_Q0_out, nB_nA__nQ0_out, nB_nA_out, nonA_out, nonB_out,
       nonQ0_out, not_1_out, not_2_out, not_3_out, not_4_out, not_5_out, not_6_out;

  Clock clock_1 (.out(clock_1_out));
  not nonB (nonB_out, B);
  not nonA (nonA_out, A);
  not nonQ0 (nonQ0_out, out_3[0]);
  or nB_nA (nB_nA_out, nonB_out, nonA_out);
  or B_nA (B_nA_out, B, nonA_out);
  or nB_A (nB_A_out, nonB_out, A);
  not not_1 (not_1_out, nB_A_out);
  not not_2 (not_2_out, nB_nA_out);
  or B_A (B_A_out, B, A);
  and A_nQ0 (A_nQ0_out, A, nonQ0_out);
  not not_3 (not_3_out, B_nA_out);
  or BxA (BxA_out, not_3_out, not_1_out);
  and BxA_nQ0 (BxA_nQ0_out, BxA_out, nonQ0_out);
  and nB_A__Q0 (nB_A__Q0_out, nB_A_out, out_3[0]);
  and B_nA__nQ0 (B_nA__nQ0_out, B_nA_out, nonQ0_out);
  and B_A__Q0 (B_A__Q0_out, B_A_out, out_3[0]);
  and nB_nA__nQ0 (nB_nA__nQ0_out, nB_nA_out, nonQ0_out);
  and B_nA_Q0 (B_nA_Q0_out, not_1_out, out_3[0]);
  not not_4 (not_4_out, nB_nA__nQ0_out);
  and nB_A_Q0 (nB_A_Q0_out, not_3_out, out_3[0]);
  or B_nA_Q0_2 (B_nA_Q0_2_out, B_nA_out, out_3[0]);
  not not_5 (not_5_out, B_nA_Q0_2_out);
  or BxA_nQ0_2 (BxA_nQ0_2_out, BxA_out, nonQ0_out);
  or B_A_nQ0 (B_A_nQ0_out, not_2_out, nonQ0_out);
  or nB_A__Q0__B_nA__nQ0 (nB_A__Q0__B_nA__nQ0_out, nB_A__Q0_out, B_nA__nQ0_out);
  or A_nQ0_B_nA_Q0 (A_nQ0_B_nA_Q0_out, A_nQ0_out, B_nA_Q0_out);
  or nB_A_Q0_A_nQ0 (nB_A_Q0_A_nQ0_out, nB_A_Q0_out, A_nQ0_out);
  Multiplexer #(.select(3)) multiplexer_1 (
    .in0(BxA_nQ0_out), .in1(nB_A__Q0__B_nA__nQ0_out), .in2(BxA_nQ0_2_out), .in3(B_A__Q0_out),
    .in4(B_nA_Q0_2_out), .in5(BxA_nQ0_out), .in6(nB_nA_out), .in7(nB_nA__nQ0_out), .out(multiplexer_1_out),
    .sel(out_3[3:1]), .en(1'b1));
  Multiplexer #(.select(3)) multiplexer_2 (
    .in0(A_nQ0_B_nA_Q0_out), .in1(1'b1), .in2(A), .in3(not_4_out), .in4(1'b1), .in5(nB_A_Q0_A_nQ0_out),
    .in6(1'b1), .in7(B_A_nQ0_out), .out(multiplexer_2_out), .sel(out_3[3:1]), .en(1'b1));
  Multiplexer #(.select(3)) multiplexer_3 (
    .in0(B), .in1(1'b0), .in2(not_3_out), .in3(1'b0), .in4(B_nA_Q0_out), .in5(1'b0), .in6(1'b1), .in7(1'b1),
    .out(multiplexer_3_out), .sel(out_3[3:1]), .en(1'b1));
  not not_6 (not_6_out, multiplexer_1_out);
  // _74163 74163_1: pin names not known; wires that end beside it: 1'b0, not_6_out, multiplexer_2_out, multiplexer_2_out, multiplexer_3_out, out_3[3], n74163_1_p7, out_3[2], n74163_1_p9, out_3[1], n74163_1_p11, out_3[0], clock_1_out, 1'b1, 1'b1
  Multiplexer #(.select(3)) multiplexer_4 (
    .in0(A), .in1(1'b0), .in2(not_5_out), .in3(1'b1), .in4(1'b1), .in5(B), .in6(1'b0), .in7(1'b0),
    .out(n74163_1_p7), .sel(out_3[3:1]), .en(1'b1));
  Multiplexer #(.select(3)) multiplexer_5 (
    .in0(B), .in1(1'b0), .in2(not_3_out), .in3(1'b1), .in4(1'b1), .in5(1'b0), .in6(1'b1), .in7(1'b1),
    .out(n74163_1_p9), .sel(out_3[3:1]), .en(1'b1));
  Multiplexer #(.select(3)) multiplexer_6 (
    .in0(A), .in1(1'b1), .in2(nonQ0_out), .in3(1'b0), .in4(B_nA_Q0_out), .in5(B), .in6(1'b1), .in7(1'b1),
    .out(n74163_1_p11), .sel(out_3[3:1]), .en(1'b1));

  // Notes on the sheet:
  //   b, a, b, a
  //   ba, rien, a, b 
  //   a, ba, ba, ba
  //   Load
  //   CE
  //   D3
  //   D2
  //   D1
  //   D0
endmodule
